// Logisim project 16-bit ALU.circ as structural Verilog
module _1_bit_ALU (
  input  in_1,
  input  in_2,
  input  [15:0] A,
  input  [15:0] B
);

  wire adder_1_cout;
  wire [15:0] adder_1_out, and_1_out, or_1_out, xor_1_out, xor_2_out;
  wire [15:1] undriven;

  assign xor_1_out = B ^ {undriven, in_1};  // XOR_Gate xor_1, 16 bits wide
  assign and_1_out = A & B;  // AND_Gate and_1, 16 bits wide
  assign or_1_out = A | B;  // OR_Gate or_1, 16 bits wide
  assign xor_2_out = A ^ B;  // XOR_Gate xor_2, 16 bits wide
  Adder #(.width(16)) adder_1 (.a(A), .b(xor_1_out), .out(adder_1_out), .cin(in_2), .cout(adder_1_cout));
  Multiplexer #(.select(2), .width(16)) multiplexer_1 (
    .in0(and_1_out), .in1(or_1_out), .in2(xor_2_out), .in3(adder_1_out));  // open: out, sel, en
  // Pins of 1 and 16 bits meet at {undriven, in_1}
endmodule
